# Fritzing sketch main (saved by Fritzing 0.9.5d)
circuit board: 20cm x 10cm

parts:
  Arduino = Arduino Nano (Rev3.0)
  openswitch = SPST Switch [package=switch-spdt_kit]
  closeSwitch = SPST Switch [package=switch-spdt]
  modeSwitch = Toggle Switch [package=THT]
  infraredSensor = fc-51 [package=THT]
  rainSensor = YL-83 Rain Sensor - Control Board
  YL-83_-_Detection_Board1 = YL-83 Rain Sensor - Detection Board
  R3_closeswitch = Resistor [tolerance=±5% resistance=10k package=THT]
  R2_openbutton = Resistor [tolerance=±5% resistance=10k package=THT]
  J1 = Power Jack [package=power_jack_slot]
  Driver1 = 28BYJ-48 Driver Module [part_number=ULN2003 package=THT]
  R4_openswitch = Resistor [tolerance=±5% resistance=10k package=THT]
  closebutton = Round Pushbutton
  R1_closebutton = Resistor [tolerance=±5% resistance=10k package=THT]
  openbutton = Round Pushbutton
  SW1 = Slide_Switch_new
  Arduino1 = Arduino Nano (Rev3.0)
  sweepServo = Basic Servo
  modeSwitch_2 = SPST Switch [package=switch-spdt_kit]
  manualcontrolSwitch = SPST Switch [package=switch-spdt_kit]
  R1_modeswitch = Resistor [tolerance=±5% resistance=10k package=THT]
  R3_sweepSwitch2 = Resistor [tolerance=±5% resistance=10k package=THT]
  R2_sweepSwitch1 = Resistor [tolerance=±5% resistance=10k package=THT]
  R5_modeswitch = Resistor [tolerance=±5% resistance=10k package=THT]
  modeLed = smd LED [color="Red (633nm)" package="1206 [SMD]"]
  LED1 = LED - 3mm [color="Red (633nm)" package="3 mm [THT]"]
  MOTOR1 = 28BYJ-48 Stepper Motor

nets:
  GND: Arduino.GND, infraredSensor.pin2, rainSensor.GND, R3_closeswitch.Pin_0, J1.GNDBREAK, Driver1.GND, R4_openswitch.Pin_0, R1_closebutton.Pin_0, Arduino1.GND, sweepServo.gnd, R1_modeswitch.Pin_0, R3_sweepSwitch2.Pin_0, R2_sweepSwitch1.Pin_0, R5_modeswitch.Pin_0, modeLed.cathode, LED1.cathode
  N1: Arduino.D2, closebutton.leg0, R1_closebutton.Pin_1
  N2: Arduino.D3, R2_openbutton.Pin_1, openbutton.leg0
  N3: Arduino.D4, closeSwitch.S, R3_closeswitch.Pin_1
  N4: Arduino.D5, openswitch.S, R4_openswitch.Pin_1
  N5: Arduino.D6, rainSensor.DO
  N6: Arduino.D7, modeSwitch.L1, R5_modeswitch.Pin_1
  N7: Arduino.D8, Driver1.IN4
  N8: Arduino.D9, Driver1.IN3
  N9: Arduino.D10, Driver1.IN2
  N10: Arduino.D11/MOSI, Driver1.IN1
  N11: Arduino.D12/MISO, infraredSensor.pin1
  VIN: Arduino.VIN, Driver1.Vmotor, SW1.pin_2, Arduino1.VIN
  5V: Arduino.5V, infraredSensor.pin3, rainSensor.VCC
  N12: Arduino.A2, LED1.anode
  N13: Arduino.3V3, openswitch.P, closeSwitch.P, modeSwitch.COM, closebutton.leg1, openbutton.leg1
  N14: rainSensor.AO, Arduino1.A1
  N15: rainSensor.POS, YL-83_-_Detection_Board1.POS
  N16: rainSensor.NEG, YL-83_-_Detection_Board1.NEG
  N17: J1.PWR, SW1.pin_1
  N18: Driver1.blue-pin, MOTOR1.BLUE
  N19: Driver1.pink-pin, MOTOR1.PINK
  N20: Driver1.yellow-pin, MOTOR1.YELLOW
  N21: Driver1.orange-pin, MOTOR1.ORANGE
  N22: Driver1.red-pin, MOTOR1.RED
  N23: Arduino1.D2, manualcontrolSwitch.S, R2_sweepSwitch1.Pin_1
  N24: Arduino1.D3, manualcontrolSwitch.O, R3_sweepSwitch2.Pin_1
  N25: Arduino1.D4, modeLed.anode
  N26: Arduino1.D8, modeSwitch_2.S, R1_modeswitch.Pin_1
  5V_2: Arduino1.5V, sweepServo.vcc
  N27: Arduino1.3V3, modeSwitch_2.P, manualcontrolSwitch.P
  N28: Arduino1.D13/SCK, sweepServo.pulse

custom parts:
  YL-83 Rain Sensor - Control Board: The YL-83 is a rain sensor that has more resistance when dry and less resistance when wet. The module runs at 5V.
  YL-83 Rain Sensor - Detection Board: The YL-83 is a rain sensor that has more resistance when dry and less resistance when wet. The module runs at 5V.
  28BYJ-48 Driver Module: ULN2003 Driver Module for the 28BYJ-48 Unipolar Stepper Motor LED A - Blue wire - Bottom coil left LED B - Pink wire - Top coil left LED C - Yellow wire - Bottom coil right LED D - Orange wire - Top coil right Common rail - red Connector pins: blue - pink - yellow - orange - red Control pins - IN1 to IN4 Power pins - GND & Vmotor (5-12V) On/Off jumper (if removed, power to motor is cut).
  Slide_Switch_new: the New two pin slide switch
